# Fritzing sketch AR07_fnd (saved by Fritzing 0.9.3b)
breadboards: 1

parts:
  부품1 = Arduino Uno (Rev3)
  7_Segment1 = 7 Segment Display
  R1 = Resistor [tolerance=±5% resistance=330 package=THT]
  R2 = Resistor [tolerance=±5% resistance=330 package=THT]
  R3 = Resistor [tolerance=±5% resistance=330 package=THT]
  R4 = Resistor [tolerance=±5% resistance=330 package=THT]
  R5 = Resistor [tolerance=±5% resistance=330 package=THT]  # not connected
  R6 = Resistor [tolerance=±5% resistance=330 package=THT]
  R7 = Resistor [tolerance=±5% resistance=330 package=THT]
  R8 = Resistor [tolerance=±5% resistance=330 package=THT]

nets:
  N1: 부품1.D8, 부품1.D7, R2.Pin_1
  N2: 부품1.D9_PWM, R7.Pin_0
  N3: 부품1.D2, R3.Pin_1
  N4: 부품1.D3_PWM, R4.Pin_1
  N5: 부품1.D4, R8.Pin_0
  N6: 부품1.D5_PWM, R6.Pin_0
  N7: 부품1.GND, 7_Segment1.Segment_F, 7_Segment1.common_anode, R1.Pin_0
  N8: 7_Segment1.Segment_G, R2.Pin_0
  N9: 7_Segment1.Segment_D, R6.Pin_1
  N10: 7_Segment1.Segment_DP, R7.Pin_1
  N11: 7_Segment1.Segment_C, R8.Pin_1
  N12: 7_Segment1.Segment_B, R4.Pin_0
  N13: 7_Segment1.Segment_A, R3.Pin_0
