# Fritzing sketch Automatic_trashcan (saved by Fritzing 0.9.3b)
breadboards: 1

parts:
  부품1 = Arduino Uno (Rev3) - ICSP
  J1 = Basic Servo
  hc-sr1 = hc-sr04

nets:
  N1: 부품1.D9_PWM, J1.pulse
  N2: 부품1.D2, hc-sr1.Trig
  N3: 부품1.D3_PWM, hc-sr1.Echo
  VCC: 부품1.5V, J1.vcc, hc-sr1.VCC
  GND: 부품1.GND, J1.gnd, hc-sr1.GND
